// Logisim project TallerLogicaCombinatorios.circ as structural Verilog: 9 circuits, main circuit sumador_simple
module sumador_simple (
  input  A,
  input  B,
  output S,
  output Cout
);

  xor xor_1 (S, A, B);
  and and_1 (Cout, A, B);

  // Notes on the sheet:
  //   Ejercicio 1
endmodule

module sumador_completo (
  input  Cin,
  input  A,
  input  B,
  output S,
  output Cout
);

  wire sumador_simple_1_cout, sumador_simple_1_s, sumador_simple_2_cout;

  sumador_simple sumador_simple_1 (.A(A), .B(B), .S(sumador_simple_1_s), .Cout(sumador_simple_1_cout));
  sumador_simple sumador_simple_2 (.A(Cin), .B(sumador_simple_1_s), .S(S), .Cout(sumador_simple_2_cout));
  or or_1 (Cout, sumador_simple_2_cout, sumador_simple_1_cout);
endmodule

module sumador_4 (
  input  Cin,
  input  [3:0] A,
  input  [3:0] B,
  output [3:0] S,
  output Cout
);

  wire sumador_completo_1_cout, sumador_completo_2_cout, sumador_completo_3_cout;

  sumador_completo sumador_completo_1 (.Cin(Cin), .A(A[0]), .B(B[0]), .S(S[0]), .Cout(sumador_completo_1_cout));
  sumador_completo sumador_completo_2 (
    .Cin(sumador_completo_1_cout), .A(A[1]), .B(B[1]), .S(S[1]), .Cout(sumador_completo_2_cout));
  sumador_completo sumador_completo_3 (
    .Cin(sumador_completo_2_cout), .A(A[2]), .B(B[2]), .S(S[2]), .Cout(sumador_completo_3_cout));
  sumador_completo sumador_completo_4 (.Cin(sumador_completo_3_cout), .A(A[3]), .B(B[3]), .S(S[3]), .Cout(Cout));
  Hex_Digit_Display hex_digit_display_1 (.value(S));  // open: dp
endmodule

module comparador_cero (
  input  [3:0] A,
  output Z
);

  wire and_1_out, and_2_out, not_1_out, not_2_out, not_3_out, not_4_out;

  not not_1 (not_1_out, A[0]);
  not not_2 (not_2_out, A[1]);
  not not_3 (not_3_out, A[2]);
  not not_4 (not_4_out, A[3]);
  and and_1 (and_1_out, not_1_out, not_2_out);
  and and_2 (and_2_out, not_3_out, not_4_out);
  and and_3 (Z, and_1_out, and_2_out);
endmodule

module sumador_flags (
  input  Cin,
  input  [3:0] A,
  input  [3:0] B,
  output [3:0] S,
  output Z,
  output N,
  output C,
  output out_8
);

  wire not_1_out, xor_1_out, xor_2_out;

  sumador_4 sumador_4_1 (.Cin(Cin), .A(A), .B(B), .S({N, S[2:0]}), .Cout(C));
  Hex_Digit_Display hex_digit_display_1 (.value({N, S[2:0]}));  // open: dp
  comparador_cero comparador_cero_1 (.A({N, S[2:0]}), .Z(Z));
  xor xor_1 (xor_1_out, N, A[3]);
  xor xor_2 (xor_2_out, A[3], B[3]);
  not not_1 (not_1_out, xor_2_out);
  and and_1 (out_8, xor_1_out, not_1_out);

  assign S[3] = N;
endmodule

module incrementador_4 (
  input  [3:0] A,
  output [3:0] S
);

  sumador_4 sumador_4_1 (.A(4'b0001), .B(A), .S(S));  // open: Cin, Cout
  Hex_Digit_Display hex_digit_display_1 (.value(S));  // open: dp
endmodule

module inversor_4 (
  input  [3:0] A,
  input  INV,
  input  [3:0] in_3,
  input  in_4,
  output [3:0] S,
  output [3:0] out_6
);

  wire sumador_simple_1_s, sumador_simple_2_s, sumador_simple_3_s, sumador_simple_4_s, sumador_simple_5_cout,
       sumador_simple_6_cout, sumador_simple_7_cout;
  wire [3:0] incrementador_4_1_s, xor_1_out;

  xor xor_1 (xor_1_out[0], in_3[0], in_4);
  xor xor_2 (xor_1_out[1], in_3[1], in_4);
  xor xor_3 (xor_1_out[2], in_3[2], in_4);
  xor xor_4 (xor_1_out[3], in_3[3], in_4);
  sumador_simple sumador_simple_1 (.A(A[0]), .B(INV), .S(sumador_simple_1_s));  // open: Cout
  sumador_simple sumador_simple_2 (.A(A[1]), .B(INV), .S(sumador_simple_2_s));  // open: Cout
  sumador_simple sumador_simple_3 (.A(A[2]), .B(INV), .S(sumador_simple_3_s));  // open: Cout
  sumador_simple sumador_simple_4 (.A(A[3]), .B(INV), .S(sumador_simple_4_s));  // open: Cout
  Multiplexer #(.width(4)) multiplexer_1 (.in0(xor_1_out), .in1(incrementador_4_1_s), .out(out_6), .sel(in_4));
  incrementador_4 incrementador_4_1 (.A(xor_1_out), .S(incrementador_4_1_s));
  sumador_simple sumador_simple_5 (.A(sumador_simple_1_s), .B(INV), .S(S[0]), .Cout(sumador_simple_5_cout));
  sumador_simple sumador_simple_6 (
    .A(sumador_simple_5_cout), .B(sumador_simple_2_s), .S(S[1]), .Cout(sumador_simple_6_cout));
  Hex_Digit_Display hex_digit_display_1 (.value(out_6));  // open: dp
  sumador_simple sumador_simple_7 (
    .A(sumador_simple_6_cout), .B(sumador_simple_3_s), .S(S[2]), .Cout(sumador_simple_7_cout));
  sumador_simple sumador_simple_8 (.A(sumador_simple_7_cout), .B(sumador_simple_4_s), .S(S[3]));  // open: Cout
  Hex_Digit_Display hex_digit_display_2 (.value(S));  // open: dp
endmodule

module ALU (
  input  [3:0] A,
  input  [3:0] B,
  input  [1:0] OP,
  output N,
  output Z,
  output V,
  output C,
  output [3:0] S
);

  wire comparador_cero_1_z;
  wire [3:0] sumador_4_1_s;

  Hex_Digit_Display hex_digit_display_1 (.value(S));  // open: dp
  sumador_4 sumador_4_1 (.A(A), .B(B), .S(sumador_4_1_s));  // open: Cin, Cout
  comparador_cero comparador_cero_1 (.A(sumador_4_1_s), .Z(comparador_cero_1_z));
  // AND_Gate and_1 has open pins: in0=comparador_cero_1_z, out=open
endmodule

module verificador (
  output [3:0] out_1,
  output [3:0] out_2,
  output [1:0] out_3,
  output halt,
  output N,
  output Z,
  output V,
  output C,
  output [3:0] res
);

  wire clock_1_out;

  Clock clock_1 (.out(clock_1_out));
  Counter #(.max('h3ff), .width(10)) counter_1 (
    .clk(clock_1_out), .carry(halt), .Q({out_3, out_2, out_1}));  // open: clr, load, up, count, D
  ALU alu_1 (.A(out_1), .B(out_2), .OP(out_3), .N(N), .Z(Z), .V(V), .C(C), .S(res));
endmodule
